# Fritzing sketch schematic-diagram (saved by Fritzing 0.9.5d)
breadboards: 1

parts:
  DHT1 = DHT22 Humidity and Temperature Sensor
  J1 = Piezo Speaker
  Mod1 = KY-026 Flame Sensor Module [package="Breakout board"]
  Mini_Water_Pump_3-6VDC1 = Mini Water Pump 3-6VDC [part_number="Mini Water Pump 3-6VDC" chip_label=IC package="DIP (Dual Inline) [THT]"]
  Mod2 = KY-019 5V Relay Module [package="Breakout board"]
  Mod3 = KY-019 5V Relay Module [package="Breakout board"]
  Part1 = Arduino Uno (Rev3)
  VCC1 = Battery

nets:
  VDD: DHT1.VDD, Mod1.+, Mod2.+, Mod3.+, Part1.5V
  N1: DHT1.DATA, Part1.D5_PWM
  GND: DHT1.GND, Mod1.G, Mod2.-, Mod3.-, Part1.GND
  N2: J1.pin1, Mini_Water_Pump_3-6VDC1.-M, VCC1.-
  N3: J1.pin2, Mod2.NO
  N4: Mod1.D0, Part1.D6_PWM
  N5: Mini_Water_Pump_3-6VDC1.+M, Mod3.NO
  N6: Mod2.S, Part1.D4
  N7: Mod2.Common, Mod3.Common, VCC1.+
  N8: Mod3.S, Part1.D7

notes:
  Relay
  Waterpump
  Buzzer
  DHT22 Sensor
  Flame Sensor

custom parts:
  KY-026 Flame Sensor Module: KY-026 Flame Sensor Module reacts in the presence of fire.
  KY-019 5V Relay Module: KY-019 5V Relay module, used to control AC circuits. (Special thanks to vanepp for fixing the PCB holes and other errors)
